# Fritzing sketch retroblue2 (saved by Fritzing 0.9.2b)
circuit board: 3.78178cm x 7.00733cm
breadboards: 1

parts:
  Y1 = Resonator [frequency="8 MHz" package=THT]
  U2 = Voltage Regulator - Variable [package="TO220 [THT]"]
  R1 = Resistor [tolerance=±5% resistance=330k package=THT]
  LED1 = LED - 5mm [color="Yellow (595nm)" package="5 mm [THT]"]
  R2 = Resistor [tolerance=±5% resistance=1k package=THT]
  S1 = Pushbutton [package="[THT]"]
  U3 = USB Connectors [package=usb-minib]
  J4 = male pin header, 6 pins [form="♂ (male)"]
  LED3 = LED - 5mm [color="Red (633nm)" package="5 mm [THT]"]
  LED4 = LED - 5mm [color="Blue (525nm)" package="5 mm [THT]"]
  R5 = Resistor [tolerance=±5% resistance=330k package=THT]
  R6 = Resistor [tolerance=±5% resistance=330k package=THT]
  R14 = Resistor [tolerance=±5% resistance=2.2k package=THT]
  J3 = screw terminal, 3 pins
  J7 = screw terminal, 3 pins
  Part1 = BC127 SMD
  J8 = screw terminal, 3 pins
  U1 = atmega328 [package=dip]
  10nF1 = Electrolytic Capacitor [capacitance=1µF package="100 mil [THT, electrolytic]"]
  10nF2 = Electrolytic Capacitor [capacitance=1µF package="100 mil [THT, electrolytic]"]
  J9 = screw terminal, 3 pins

nets:
  N1: Y1.0, U1.XLAT2
  GND: Y1.GND, U2.OUT, R1.Pin_0, S1.Pin_1, S1.Pin_2, U3.GND, J4.pin6, R5.Pin_1, R6.Pin_1, J7.pin2, Part1.GND#36, Part1.GND#58, Part1.GND#59, Part1.GND#61, J8.pin2, J8.pin3, U1.GND, 10nF1.-, 10nF2.-
  N2: Y1.pin_1, U1.XLAT1
  N3: U2.ADJ, 10nF1.+
  N4: U2.IN, R2.Pin_1, U3.VBUS, J4.pin4, Part1.VBAT_SENSE, Part1.VCHG, Part1.VDD_PADS, Part1.V_BAT, U1.VCC, U1.AVCC, U1.AREF, 10nF2.+, J9.pin3
  N5: R1.Pin_1, LED1.anode
  N6: LED1.cathode, U1.D13
  N7: R2.Pin_0, S1.Pin_3, S1.Pin_4, U1.RESET
  N8: U3.D+, U1.D0_(RX)
  N9: U3.D-, U1.D1_(TX)
  N10: J4.pin1, Part1.DTR
  N11: J4.pin2, Part1.RX, U1.D11_(PWM)
  N12: J4.pin3, Part1.TX, U1.D12
  N13: J4.pin5, Part1.CTS
  N14: LED3.cathode, Part1.LED2
  N15: LED3.anode, R5.Pin_0
  N16: LED4.cathode, Part1.LED1
  N17: LED4.anode, R6.Pin_0
  N18: R14.Pin_0, Part1.MIC_BIAS_A, Part1.MIC_LP
  N19: R14.Pin_1, J3.pin1, Part1.MIC_LN
  N20: J3.pin2, Part1.GND#24, Part1.CAP_SEN_2
  N21: J3.pin3, Part1.SP_RP
  N22: J7.pin1, U1.D4
  N23: J7.pin3, U1.D3_(PWM)
  N24: Part1.SP_RN, Part1.GND#33
  N25: J8.pin1, U1.D2
  N26: U1.D9_(PWM), J9.pin2
  N27: U1.D10_(PWM), J9.pin1

notes:
  RETROBLUE
